# Fritzing sketch Home Auto (saved by Fritzing 0.9.3b)
breadboards: 1

parts:
  Part1 = Arduino Uno (Rev3)
  M1 = fc-51 [package=THT]
  M2 = fc-51 [package=THT]
  KY-1 = Keyes Relay [package=THT]
  KY-2 = Keyes Relay [package=THT]
  KY-3 = Keyes Relay [package=THT]
  KY-4 = Keyes Relay [package=THT]
  Grove_Touch_Sensor(P)1 = Grove Touch Sensor (P)
  J1 = Piezo Speaker

nets:
  N1: Part1.A0, M2.pin1
  N2: Part1.A1, M1.pin1
  N3: Part1.D8, Grove_Touch_Sensor(P)1.SIG
  N4: Part1.D9_PWM, J1.pin2
  N5: Part1.D5_PWM, KY-1.signal
  N6: Part1.D6_PWM, KY-2.signal
  N7: Part1.D7, KY-3.signal
  5V: Part1.5V, M1.pin3, M2.pin3, KY-1.power, KY-2.power, KY-3.power, KY-4.power, Grove_Touch_Sensor(P)1.VCC
  GND: Part1.GND, M1.pin2, M2.pin2, KY-1.ground, KY-2.ground, KY-3.ground, KY-4.ground, Grove_Touch_Sensor(P)1.GND, J1.pin1

custom parts:
  Keyes Relay: The Keyes 5V relay module is suitable for SCM development, home appliance control. It uses a 5V~12V TIL control signal which can control DC / AC signal.
  Grove Touch Sensor (P): Touch sensor, Grove connector, panel mount.
